# Fritzing sketch LCDTinySerial (saved by Fritzing 0.9.2b)
perfboards: 1

parts:
  U1 = attiny85 [package=dip]
  U2 = 74HC595 SMD [package="SO16 [SMD]"]
  U3 = LCD-16X2 [package=lcd-16x2_noholes]
  J1 = female pin header, 16 pins [form="♀ (female)"]
  U4 = POT [package=3362u]
  Power_plug1 = Power plug
  J2 = female pin header, 3 pins [form="♀ (female)"]
  R1 = Resistor [tolerance=±5% resistance=220 package="2512 [SMD]"]

nets:
  N1: U1.Pin_2, J2.pin1
  N2: U1.Pin_3, J2.pin2
  N3: U1.Pin_4, J2.pin3
  N4: U1.Pin_5, U2.DS
  N5: U1.Pin_6, U2.ST_CP
  N6: U1.Pin_7, U2.SH_CP
  VCC: U1.Pin_8, U2.VCC, Power_plug1.VCC, R1.Pin_1
  N7: U2.Q1, U3.DB7, J1.pin14
  N8: U2.Q2, U3.DB6, J1.pin13
  N9: U2.Q3, U3.DB5, J1.pin12
  N10: U2.Q4, U3.DB4, J1.pin11
  VSS: U2.OE, U3.VSS, U3.K, J1.pin5, J1.pin16, Power_plug1.GND
  N11: U3.A, J1.pin15, R1.Pin_0
  N12: J1.pin3, U4.S
